# Fritzing sketch DotStar-Breadboard (saved by Fritzing 0.9.3b)
breadboards: 1

parts:
  Raspberry_Pi_1 = Raspberry Pi 3 [part_number=RPI-3-V1.2]
  JACK1 = 2.1mm Barrel Jack with Terminal Block
  DOTSTAR1 = DotStar Strip -- Black (60/m) [part_number=2239]
  U1_1 = 74x125 [part_number=74x125 package="DIP (Dual Inline) [THT]"]  # not connected
  U1_3 = 74x125 [part_number=74x125 package="DIP (Dual Inline) [THT]"]  # not connected
  part = 74x125 [part_number=74x125 package="DIP (Dual Inline) [THT]"]  # not connected
  U1_2 = 74x125 [part_number=74x125 package="DIP (Dual Inline) [THT]"]  # not connected
  U1_4 = 74x125 [part_number=74x125 package="DIP (Dual Inline) [THT]"]  # not connected
  U1 = 74x125 [part_number=74AHCT125 package="DIP (Dual Inline) [THT]"]

nets:
  N1: Raspberry_Pi_1.GIPO10, U1.connector1
  N2: Raspberry_Pi_1.GIPO11, U1.connector4
  GND: Raspberry_Pi_1.GND, JACK1.NEG, DOTSTAR1.GND, U1.connector0, U1.connector3, U1.connector6
  N3: JACK1.POS, DOTSTAR1.+5V, U1.connector13
  N4: DOTSTAR1.DI, U1.connector2
  N5: DOTSTAR1.CI, U1.connector5

notes:
  +5V DC

custom parts:
  DotStar Strip -- Black (60/m): NeopixelDotStar Strip, Black, 60 pixels per meter.
  74x125: 74x125 quad tristate buffer active low enable. The 74ahc125 variety is useful as a level translator as the inputs are 5V tolorant when run with a VCC of 3.3V (and will thus take a 5V signal in and provide a 3.3V signal out.) As well this part uses schematic subparts so you can drag each of the 4 gates to a different place in schematic view. Note having many (around 10 or more) subpart parts in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
  74x125: 74x125 quad tristate buffer active low enable. The 74ahc125 variety is useful as a level translator as the inputs are 5V tolorant when run with a VCC of 3.3V (and will thus take a 5V signal in and provide a 3.3V signal out.) As well this part uses schematic subparts so you can drag each of the 4 gates to a different place in schematic view. Note having many (around 10 or more) subpart parts in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
  74x125: 74x125 quad tristate buffer active low enable. The 74ahc125 variety is useful as a level translator as the inputs are 5V tolorant when run with a VCC of 3.3V (and will thus take a 5V signal in and provide a 3.3V signal out.) As well this part uses schematic subparts so you can drag each of the 4 gates to a different place in schematic view. Note having many (around 10 or more) subpart parts in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
  74x125: 74x125 quad tristate buffer active low enable. The 74ahc125 variety is useful as a level translator as the inputs are 5V tolorant when run with a VCC of 3.3V (and will thus take a 5V signal in and provide a 3.3V signal out.) As well this part uses schematic subparts so you can drag each of the 4 gates to a different place in schematic view. Note having many (around 10 or more) subpart parts in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
  74x125: 74x125 quad tristate buffer active low enable. The 74ahc125 variety is useful as a level translator as the inputs are 5V tolorant when run with a VCC of 3.3V (and will thus take a 5V signal in and provide a 3.3V signal out.) As well this part uses schematic subparts so you can drag each of the 4 gates to a different place in schematic view. Note having many (around 10 or more) subpart parts in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
  74x125: 74x125 quad tristate buffer active low enable. The 74ahc125 variety is useful as a level translator as the inputs are 5V tolorant when run with a VCC of 3.3V (and will thus take a 5V signal in and provide a 3.3V signal out.) As well this part uses schematic subparts so you can drag each of the 4 gates to a different place in schematic view. Note having many (around 10 or more) subpart parts in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
